# Fritzing sketch blu-pi-display (saved by Fritzing 0.9.3b)
breadboards: 1

parts:
  U1 = attiny85 [package=dip]
  JP1 = Header 8 [package=1x08_smd_alt]
  JP4 = Header 1 [package=1x01_offset]
  JP5 = Header 1 [package=1x01_offset]
  JP6 = Header 1 [package=1x01_offset]
  S2 = Momentary Switch [package=ksa_sealed_tac_switch]
  S3 = Momentary Switch [package=ksa_sealed_tac_switch]
  S4 = Momentary Switch [package=ksa_sealed_tac_switch]
  R1 = Resistor [tolerance=±5% resistance=220k package="0805 [SMD]"]
  R2 = Resistor [tolerance=±5% resistance=220k package="0805 [SMD]"]
  JP7 = Header 1 [package=1x01_offset]
  Part1 = OLED Monochrome 128x64 1.3 inch [part_number=938]  # not connected
  S5 = Reed switch [package=THT]  # not connected
  S6 = Reed switch [package=THT]  # not connected
  JP11 = Header 1 [part_number=pin-header-vi package=1x01_offset]
  JP12 = Header 1 [package=1x01_offset]
  JP13 = Header 1 [package=1x01_offset]
  JP14 = Header 1 [package=1x01_offset]
  R3 = Resistor [tolerance=±5% resistance=220k package="0805 [SMD]"]

nets:
  N1: U1.Pin_2, JP5.1
  N2: U1.Pin_3, JP4.1
  N3: U1.Pin_4, JP1.8, JP6.1, S2.1, S2.2, S3.1, S3.2, S4.1, S4.2, JP12.1
  N4: U1.Pin_5, JP1.1, JP13.1
  N5: U1.Pin_7, JP1.2, JP14.1
  N6: U1.Pin_8, JP1.7, R1.Pin_0, R2.Pin_0, JP11.1, R3.Pin_0
  N7: JP1.4, JP7.1
  N8: S2.4, R3.Pin_1
  N9: S3.3, S3.4, R1.Pin_1
  N10: S4.3, S4.4, R2.Pin_1

notes:
  blu-pi display

custom parts:
  OLED Monochrome 128x64 1.3 inch: These displays are small, only about 1.3" diagonal, but very readable due to the high contrast of an OLED display. This display is made of 128x64 individual white OLED pixels, each one is turned on or off by the controller chip. Because the display makes its own light, no backlight is required. This reduces the power required to run the OLED and is why the display has such high contrast; we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
